// Logisim project LC-2200-16.circ as structural Verilog: 3 circuits, main circuit main
module main (
  input  LDPC,
  input  LDA,
  input  LDB,
  input  LDIR,
  input  [1:0] in_5,
  input  DrPC,
  input  DrALU,
  input  DrREG
);

  wire CLK;
  wire [15:0] A_q, ALU_out, B_q, controlled_buffer_1_out, IR_q, PC_q, ram_1_data;

  Clock clock_1 (.out(CLK));
  Register #(.width(16)) PC (.D(controlled_buffer_1_out), .en(LDPC), .Q(PC_q), .clk(CLK));  // open: clr
  assign controlled_buffer_1_out = DrPC ? PC_q : 16'bz;  // Controlled_Buffer controlled_buffer_1
  Register #(.width(16)) A (.D(controlled_buffer_1_out), .en(LDA), .Q(A_q), .clk(CLK));  // open: clr
  Register #(.width(16)) B (.D(controlled_buffer_1_out), .en(LDB), .Q(B_q), .clk(CLK));  // open: clr
  ALU ALU (.func(in_5), .A(A_q), .B(B_q), .Out(ALU_out));
  assign controlled_buffer_1_out = DrALU ? ALU_out : 16'bz;  // Controlled_Buffer controlled_buffer_2
  RAM #(.addrWidth(16), .dataWidth(16)) ram_1 (
    .addr(controlled_buffer_1_out), .data(ram_1_data));  // open: sel, clk, ld, clr
  assign controlled_buffer_1_out = DrREG ? ram_1_data : 16'bz;  // Controlled_Buffer controlled_buffer_3
  Register #(.width(16)) IR (.D(controlled_buffer_1_out), .en(LDIR), .Q(IR_q), .clk(CLK));  // open: clr
endmodule

module ALU (
  input  [15:0] A,
  input  [15:0] B,
  input  [1:0] func,
  output [15:0] Out
);

  wire [15:0] adder_1_out, adder_2_out, nand_1_out, subtractor_1_out;

  Adder #(.width(16)) adder_1 (.a(A), .b(B), .out(adder_1_out));  // open: cin, cout
  assign nand_1_out = ~(A & B);  // NAND_Gate nand_1, 16 bits wide
  Subtractor #(.width(16)) subtractor_1 (.a(A), .b(B), .out(subtractor_1_out));  // open: bin, bout
  Adder #(.width(16)) adder_2 (.a(A), .b(16'h1), .out(adder_2_out));  // open: cin, cout
  Multiplexer #(.select(2), .width(16)) multiplexer_1 (
    .in0(adder_1_out), .in1(nand_1_out), .in2(subtractor_1_out), .in3(adder_2_out), .out(Out), .sel(func));  // open: en
endmodule

module RegFile (
  input  [3:0] Regno,
  input  WrMEM,
  input  CLK,
  output [15:0] Dout
);

  wire [15:0] register_1_q, register_2_q, register_3_q, register_4_q, register_5_q, register_6_q,
       register_7_q, register_8_q, register_9_q, register_10_q, register_11_q, register_12_q, register_13_q,
       register_14_q, register_15_q, register_16_q;

  Register #(.width(16)) register_1 (.en(WrMEM), .Q(register_1_q), .clk(CLK));  // open: D, clr
  Register #(.width(16)) register_2 (.en(WrMEM), .Q(register_2_q), .clk(CLK));  // open: D, clr
  Register #(.width(16)) register_3 (.en(WrMEM), .Q(register_3_q), .clk(CLK));  // open: D, clr
  Register #(.width(16)) register_4 (.en(WrMEM), .Q(register_4_q), .clk(CLK));  // open: D, clr
  Register #(.width(16)) register_5 (.en(WrMEM), .Q(register_5_q), .clk(CLK));  // open: D, clr
  Register #(.width(16)) register_6 (.en(WrMEM), .Q(register_6_q), .clk(CLK));  // open: D, clr
  Register #(.width(16)) register_7 (.en(WrMEM), .Q(register_7_q), .clk(CLK));  // open: D, clr
  Register #(.width(16)) register_8 (.en(WrMEM), .Q(register_8_q), .clk(CLK));  // open: D, clr
  Register #(.width(16)) register_9 (.en(WrMEM), .Q(register_9_q), .clk(CLK));  // open: D, clr
  Register #(.width(16)) register_10 (.en(WrMEM), .Q(register_10_q), .clk(CLK));  // open: D, clr
  Register #(.width(16)) register_11 (.en(WrMEM), .Q(register_11_q), .clk(CLK));  // open: D, clr
  Register #(.width(16)) register_12 (.en(WrMEM), .Q(register_12_q), .clk(CLK));  // open: D, clr
  Register #(.width(16)) register_13 (.en(WrMEM), .Q(register_13_q), .clk(CLK));  // open: D, clr
  Register #(.width(16)) register_14 (.en(WrMEM), .Q(register_14_q), .clk(CLK));  // open: D, clr
  Register #(.width(16)) register_15 (.en(WrMEM), .Q(register_15_q), .clk(CLK));  // open: D, clr
  Register #(.width(16)) register_16 (.en(WrMEM), .Q(register_16_q), .clk(CLK));  // open: D, clr
  Multiplexer #(.select(4), .width(16)) multiplexer_1 (
    .in0(register_1_q), .in1(register_5_q), .in2(register_9_q), .in3(register_13_q), .in4(register_2_q),
    .in5(register_6_q), .in6(register_10_q), .in7(register_14_q), .in8(register_3_q), .in9(register_7_q),
    .in10(register_11_q), .in11(register_15_q), .in12(register_4_q), .in13(register_8_q),
    .in14(register_12_q), .in15(register_16_q), .out(Dout), .sel(Regno));  // open: en

  // Other names for the same wires on the sheet: WE = WrMEM
endmodule
