// Logisim project Pierce_Clayton.circ as structural Verilog
module main (
);

  wire CLK, WrREG;
  wire [1:0] func, undriven;
  wire [3:0] OP;
  wire [23:0] adder_1_out, adder_2_out, IF_RR_addout, multiplexer_1_out, PC_q, sred_1_dout, undriven_2,
       undriven_3;
  wire [27:0] IF_RR_imout;
  wire [31:0] alu_1_out, dual_ported_register_file_1_out1, dual_ported_register_file_1_out2,
       multiplexer_2_out, multiplexer_3_out, ram_1_data, SEXT_dout, undriven_4, undriven_5, undriven_6,
       undriven_7;

  Register #(.width(24)) PC (.D(multiplexer_1_out), .Q(PC_q), .clk(CLK));  // open: en, clr
  Adder #(.width(24)) adder_1 (.a(PC_q), .b(24'h1), .out(adder_1_out));  // open: cin, cout
  Clock clock_1 (.out(CLK));
  RAM #(.addrWidth(24), .dataWidth(32)) ram_1 (.addr(PC_q), .data(ram_1_data), .clk(CLK));  // open: sel, ld, clr
  Multiplexer #(.select(2), .width(24)) multiplexer_1 (
    .in0(adder_1_out), .in1(adder_2_out), .out(multiplexer_1_out), .sel(undriven));  // open: in2, in3, en
  IF_IDRR_Buffer IF_RR (
    .ADDin(adder_1_out), .IMin(ram_1_data), .CLK(CLK), .ADDout(IF_RR_addout), .IMout({OP, IF_RR_imout}));
  SEXT SEXT (.Din({OP, IF_RR_imout}), .Dout(SEXT_dout));
  Dual_Ported_Register_File dual_ported_register_file_1 (
    .CLK(CLK), .WrREGNO(IF_RR_imout[27:24]), .RdREGNO1(IF_RR_imout[23:20]), .RdREGNO2(IF_RR_imout[3:0]),
    .INPUT(multiplexer_3_out), .OUT1(dual_ported_register_file_1_out1),
    .OUT2(dual_ported_register_file_1_out2), .WrEN(WrREG));
  IDRR_EX_Buffer idrr_ex_buffer_1 (
    .RyIn(dual_ported_register_file_1_out1), .RzIn(dual_ported_register_file_1_out2), .SEXTin(SEXT_dout),
    .CLK(CLK));  // open: RyOut, RzOut, SEXTout
  Adder #(.width(24)) adder_2 (.a(undriven_2), .b(undriven_3), .out(adder_2_out));  // open: cin, cout
  Multiplexer #(.width(32)) multiplexer_2 (.in1(undriven_4), .out(multiplexer_2_out));  // open: in0, sel, en
  ALU alu_1 (.FUNC(func), .A(undriven_5), .B(multiplexer_2_out), .OUT(alu_1_out));
  SRED sred_1 (.Din(undriven_6), .Dout(sred_1_dout));
  RAM #(.addrWidth(24), .dataWidth(32), .bus("separate")) ram_2 (
    .addr(sred_1_dout), .din(undriven_7), .clk(CLK));  // open: data, str, sel, ld, clr
  Multiplexer #(.width(32)) multiplexer_3 (.out(multiplexer_3_out));  // open: in0, in1, sel, en

  // Notes on the sheet:
  //   Go through register?
endmodule

module Dual_Ported_Register_File (
  input  CLK,
  input  WrEN,
  input  [3:0] WrREGNO,
  input  [3:0] RdREGNO1,
  input  [3:0] RdREGNO2,
  input  [31:0] INPUT,
  output [31:0] OUT1,
  output [31:0] OUT2
);

  wire En_a0, En_a1, En_a2, En_a3, En_a4, En_at, En_fp, En_k0, En_ra, En_s0, En_s1, En_s2, En_s3, En_sp,
       En_v0;
  wire [31:0] a0, a1, a2, a3, a4, at, fp, k0, ra, s0, s1, s2, s3, sp, v0, zero;

  Decoder #(.select(4), .disabled(0)) decoder_1 (
    .out1(En_at), .out2(En_v0), .out3(En_a0), .out4(En_a1), .out5(En_a2), .out6(En_a3), .out7(En_a4),
    .out8(En_s0), .out9(En_s1), .out10(En_s2), .out11(En_s3), .out12(En_k0), .out13(En_sp), .out14(En_fp),
    .out15(En_ra), .sel(WrREGNO));  // open: out0, en
  Register #(.width(32)) u_zero (.D(INPUT), .en(1'b0), .Q(zero), .clk(CLK));  // open: clr
  Register #(.width(32)) u_at (.D(INPUT), .en(En_at), .Q(at), .clk(CLK));  // open: clr
  Register #(.width(32)) u_v0 (.D(INPUT), .en(En_v0), .Q(v0), .clk(CLK));  // open: clr
  Register #(.width(32)) u_a0 (.D(INPUT), .en(En_a0), .Q(a0), .clk(CLK));  // open: clr
  Register #(.width(32)) u_a1 (.D(INPUT), .en(En_a1), .Q(a1), .clk(CLK));  // open: clr
  Register #(.width(32)) u_a2 (.D(INPUT), .en(En_a2), .Q(a2), .clk(CLK));  // open: clr
  Register #(.width(32)) u_a3 (.D(INPUT), .en(En_a3), .Q(a3), .clk(CLK));  // open: clr
  Register #(.width(32)) u_a4 (.en(En_a4), .Q(a4), .clk(CLK));  // open: D, clr
  Multiplexer #(.select(4), .width(32), .disabled(0), .enable("false")) multiplexer_1 (
    .in0(zero), .in1(at), .in2(v0), .in3(a0), .in4(a1), .in5(a2), .in6(a3), .in7(a4), .in8(s0), .in9(s1),
    .in10(s2), .in11(s3), .in12(k0), .in13(sp), .in14(fp), .in15(ra), .out(OUT2), .sel(RdREGNO2));
  Register #(.width(32)) u_s0 (.D(INPUT), .en(En_s0), .Q(s0), .clk(CLK));  // open: clr
  Register #(.width(32)) u_s1 (.D(INPUT), .en(En_s1), .Q(s1), .clk(CLK));  // open: clr
  Register #(.width(32)) u_s2 (.D(INPUT), .en(En_s2), .Q(s2), .clk(CLK));  // open: clr
  Register #(.width(32)) u_s3 (.en(En_s3), .Q(s3), .clk(CLK));  // open: D, clr
  Register #(.width(32)) u_k0 (.D(INPUT), .en(En_k0), .Q(k0), .clk(CLK));  // open: clr
  Register #(.width(32)) u_sp (.D(INPUT), .en(En_sp), .Q(sp), .clk(CLK));  // open: clr
  Register #(.width(32)) u_fp (.D(INPUT), .en(En_fp), .Q(fp), .clk(CLK));  // open: clr
  Register #(.width(32)) u_ra (.en(En_ra), .Q(ra), .clk(CLK));  // open: D, clr
  Multiplexer #(.select(4), .width(32), .disabled(0), .enable("false")) multiplexer_2 (
    .in0(zero), .in1(at), .in2(v0), .in3(a0), .in4(a1), .in5(a2), .in6(a3), .in7(a4), .in8(s0), .in9(s1),
    .in10(s2), .in11(s3), .in12(k0), .in13(sp), .in14(fp), .in15(ra), .out(OUT1), .sel(RdREGNO1));

  // Notes on the sheet:
  //   DO NOT MODIFY THIS FILE
endmodule

module IF_IDRR_Buffer (
  input  [23:0] ADDin,
  input  [31:0] IMin,
  input  CLK,
  output [23:0] ADDout,
  output [31:0] IMout
);

  Register #(.width(24)) register_1 (.D(ADDin), .Q(ADDout), .clk(CLK));  // open: en, clr
  Register #(.width(32)) register_2 (.D(IMin), .Q(IMout), .clk(CLK));  // open: en, clr
endmodule

module IDRR_EX_Buffer (
  input  [31:0] RyIn,
  input  [31:0] RzIn,
  input  [31:0] SEXTin,
  input  CLK,
  output [31:0] RyOut,
  output [31:0] RzOut,
  output [31:0] SEXTout
);

  Register #(.width(32)) register_1 (.D(RyIn), .Q(RyOut), .clk(CLK));  // open: en, clr
  Register #(.width(32)) register_2 (.D(RzIn), .Q(RzOut), .clk(CLK));  // open: en, clr
  Register #(.width(32)) register_3 (.D(SEXTin), .Q(SEXTout), .clk(CLK));  // open: en, clr
endmodule

module ALU (
  input  [1:0] FUNC,
  input  [31:0] A,
  input  [31:0] B,
  output [31:0] OUT
);

  wire [31:0] adder_1_out, adder_2_out, nand_1_out, subtractor_1_out;

  Adder #(.width(32)) adder_1 (.a(A), .b(B), .out(adder_1_out), .cin(1'b0));  // open: cout
  assign nand_1_out = ~(A & B);  // NAND_Gate nand_1, 32 bits wide
  Subtractor #(.width(32)) subtractor_1 (.a(A), .b(B), .out(subtractor_1_out), .bin(1'b0));  // open: bout
  Adder #(.width(32)) adder_2 (.a(A), .b(B), .out(adder_2_out), .cin(1'b1));  // open: cout
  Multiplexer #(.select(2), .width(32), .disabled(0), .enable("false")) multiplexer_1 (
    .in0(adder_1_out), .in1(nand_1_out), .in2(subtractor_1_out), .in3(adder_2_out), .out(OUT), .sel(FUNC));

  // Notes on the sheet:
  //   DO NOT MODIFY THIS
endmodule

module SEXT (
  input  [31:0] Din,
  output [31:0] Dout
);


  assign Dout = {{13{Din[19]}}, Din[18:0]};
endmodule

module SRED (
  input  [31:0] Din,
  output [23:0] Dout
);


  assign Dout = Din[23:0];
endmodule
